# Fritzing sketch luminaria-rgb (saved by Fritzing 0.5.2b)
breadboards: 1

parts:
  Arduino1 = Arduino
  LED-R = Red LED - 5mm [package="5 mm [THT]"]
  LED-G = Red LED - 5mm [package="5 mm [THT]"]
  LED-B = Red LED - 5mm [package="5 mm [THT]"]

nets:
  N1: Arduino1.GND, LED-R.cathode, LED-G.cathode, LED-B.cathode
  N2: Arduino1.D9, LED-B.anode
  N3: Arduino1.D5, LED-G.anode
  N4: Arduino1.D3, LED-R.anode

notes:
  Arduino com Shield Ethernet alimentado por bateria de 9V
